// Logisim project logik- 0.4 16 bit.circ as structural Verilog
module main (
  input  [15:0] in_1,
  input  [15:0] in_2
);

  wire activ, and_1_out, b_alu, bit_extender_2_out, brnh_on, Button_2_out, Button_4_out, Button_5_out,
       Button_6_out, clk, clock_1_out, clock_2_out, clock_3_out, comparator_1_eq, comparator_2_eq,
       comparator_4_eq, counter_2_carry, crg, hlt, hub_1_one, hub_1_output_1, hub_1_output_2, hub_1_output_3,
       hub_1_output_4, hub_1_output_5, hub_1_output_6, hub_1_output_7, hub_1_output_8, hub_1_output_9,
       hub_1_output_10, hub_1_output_11, hub_1_output_12, hub_1_output_13, hub_1_output_14, hub_1_output_15,
       hub_1_output_16, hub_1_output_17, hub_1_output_18, hub_1_output_19, hub_1_output_20, hub_1_output_21,
       hub_1_output_22, hub_1_output_23, hub_1_output_24, hub_1_output_25, hub_1_output_26, hub_1_output_27,
       hub_1_output_28, hub_1_output_29, hub_1_output_30, I_port_on, inst_hub_1_io_port, inst_hub_1_reg0_6,
       inst_hub_1_reg7_14, inst_hub_1_reg15_21, IO_reg, multiplexer_1_out, multiplexer_2_out,
       multiplexer_4_out, multiplexer_9_out, multiplexer_12_out, multiplexer_20_out, or_1_out, or_2_out,
       or_3_out, or_5_out, or_6_out, or_7_out, or_8_out, or_9_out, or_10_out, pc_jmp, ram_addr, ram_write,
       rgb_video_1_p1, s_r_ff_1_q, summ_1_minus, summ_1_plus, summ_1_zero, zero_flag;
  wire [1:0] inst_hub_1_reg_data_cntrl;
  wire [2:0] datamode_bus;
  wire [3:0] bit_extender_8_out, bits48_51, bits60_63;
  wire [4:0] joystick_1_x, joystick_1_y, rgb_video_1_p4, rgb_video_1_p5;
  wire [6:0] bit_extender_1_out, keyboard_1_data;
  wire [7:0] bit_extender_6_out, bit_extender_7_out, counter_3_q, counter_4_q, demultiplexer_1_out1,
       demultiplexer_1_out2, DipSwitch_3_sw8, rgb_video_1_p3, terminal_acii, terminal_clear, undriven_2;
  wire [15:0] bit_extender_9_out, bit_extender_10_out, bits0_15, bits16_31, bits32_47, counter_1_q, I_port,
       keyboard_acii_inp, multiplexer_3_out, multiplexer_5_out, multiplexer_6_out, multiplexer_7_out,
       multiplexer_8_out, multiplexer_10_out, multiplexer_13_out, multiplexer_15_out, multiplexer_16_out,
       multiplexer_17_out, multiplexer_18_out, multiplexer_19_out, multiplexer_21_out, RAM_1_dout,
       regnew_1_aout, regnew_1_bout, summ_1_regaout, summ_1_regbout, summ_1_resultout, undriven, undriven_3;
  wire [31:0] DipSwitch_1_sw24;
  wire [59:52] ROM_1_data;

  Clock clock_1 (.out(clock_1_out));
  Clock clock_2 (.out(clock_2_out));
  trigger trigger_1 ();  // open: inp1, input1, write2, reset2, write1, dreset, Output_bus_1, Output_bus_2
  Multiplexer multiplexer_1 (.in0(clock_2_out), .in1(1'b0), .out(multiplexer_1_out), .sel(multiplexer_4_out));
  not not_1 (clk, multiplexer_1_out);
  or or_1 (or_1_out, pc_jmp, multiplexer_2_out);
  Multiplexer multiplexer_2 (.in0(1'b0), .in1(zero_flag), .out(multiplexer_2_out), .sel(brnh_on));
  DotMatrix #(.matrixcols(31), .matrixrows(1)) DotMatrix_1 (
    .col0(hub_1_output_30), .col1(hub_1_output_29), .col2(hub_1_output_28), .col3(hub_1_output_27),
    .col4(hub_1_output_26), .col5(hub_1_output_25), .col6(hub_1_output_24), .col7(hub_1_output_23),
    .col8(hub_1_output_22), .col9(hub_1_output_21), .col10(hub_1_output_20), .col11(hub_1_output_19),
    .col12(hub_1_output_18), .col13(hub_1_output_17), .col14(hub_1_output_16), .col15(hub_1_output_15),
    .col16(hub_1_output_14), .col17(hub_1_output_13), .col19(hub_1_output_11), .col20(hub_1_output_10),
    .col21(hub_1_output_9), .col22(hub_1_output_8), .col23(hub_1_output_7), .col24(hub_1_output_6),
    .col25(hub_1_output_5), .col26(hub_1_output_4), .col27(hub_1_output_3), .col28(hub_1_output_2),
    .col29(hub_1_output_1), .col30(hub_1_one));  // open: col18
  Button Button_2 (.out(Button_2_out));
  Counter #(.max('hffff), .width(16)) counter_1 (
    .clr(Button_2_out), .load(and_1_out), .count(multiplexer_1_out), .clk(multiplexer_1_out),
    .D(multiplexer_3_out), .Q(counter_1_q));  // open: up, carry
  and and_1 (and_1_out, clk, or_1_out);
  Multiplexer #(.width(16)) multiplexer_3 (.in0(undriven), .in1(bits32_47), .out(multiplexer_3_out), .sel(or_2_out));
  or or_2 (or_2_out, pc_jmp, brnh_on);
  Bit_Extender #(.out_width(7)) bit_extender_1 (.in(terminal_acii), .out(bit_extender_1_out));
  TTY #(.cols(64), .rows(25)) tty_1 (.data(bit_extender_1_out), .clk(clk), .we(1'b1), .clr(or_3_out));
  Counter #(.max('h7)) counter_2 (.carry(counter_2_carry), .clk(clk));  // open: load, D, count, Q, up, clr
  Bit_Extender #(.out_width(1), .\type ("zero")) bit_extender_2 (.in(terminal_clear), .out(bit_extender_2_out));
  or or_3 (or_3_out, bit_extender_2_out, Button_5_out);
  Keyboard #(.trigger("falling")) keyboard_1 (
    .clk(counter_2_carry), .re(1'b1), .clr(Button_6_out), .data(keyboard_1_data));  // open: avail
  Button Button_6 (.out(Button_6_out));
  hub hub_1 (
    .otpo(undriven_2), .one(hub_1_one), .Output_1(hub_1_output_1), .Output_2(hub_1_output_2),
    .Output_3(hub_1_output_3), .Output_4(hub_1_output_4), .Output_5(hub_1_output_5),
    .Output_6(hub_1_output_6), .Output_7(hub_1_output_7), .Output_8(hub_1_output_8),
    .Output_9(hub_1_output_9), .Output_10(hub_1_output_10), .Output_11(hub_1_output_11),
    .Output_12(hub_1_output_12), .Output_13(hub_1_output_13), .Output_14(hub_1_output_14),
    .Output_15(hub_1_output_15), .Output_16(hub_1_output_16), .Output_17(hub_1_output_17),
    .Output_18(hub_1_output_18), .Output_19(hub_1_output_19), .Output_20(hub_1_output_20),
    .Output_21(hub_1_output_21), .Output_22(hub_1_output_22), .Output_23(hub_1_output_23),
    .Output_24(hub_1_output_24), .Output_25(hub_1_output_25), .Output_26(hub_1_output_26),
    .Output_27(hub_1_output_27), .Output_28(hub_1_output_28), .Output_29(hub_1_output_29),
    .Output_30(hub_1_output_30));
  Button Button_5 (.out(Button_5_out));
  ROM #(.addrWidth(16), .dataWidth(64)) ROM_1 (
    .addr(counter_1_q), .data({bits60_63, ROM_1_data, bits48_51, bits32_47, bits16_31, bits0_15}));
  Multiplexer multiplexer_4 (.in0(hlt), .in1(1'b0), .out(multiplexer_4_out), .sel(Button_2_out));
  // Probe on keyboard_acii_inp
  assign keyboard_acii_inp = {{9{1'b0}}, keyboard_1_data};  // Bit_Extender bit_extender_3
  Clock clock_3 (.out(clock_3_out));
  // RGB_Video #(.cursor("No Cursor"), .height(32), .scale(8), .width(32)) rgb_video_1: pin names not known; wires that end beside it: rgb_video_1_p1, clk, rgb_video_1_p3[0], rgb_video_1_p4, rgb_video_1_p5, 24'hf5a700
  Multiplexer #(.width(16)) multiplexer_5 (
    .in0({16{1'b0}}), .in1(bits0_15), .out(multiplexer_5_out), .sel(inst_hub_1_reg0_6));
  Multiplexer #(.width(16)) multiplexer_6 (.in0({16{1'b0}}), .in1(bits16_31), .out(multiplexer_6_out), .sel(or_5_out));
  Multiplexer #(.width(16)) multiplexer_7 (
    .in0({16{1'b0}}), .in1(bits32_47), .out(multiplexer_7_out), .sel(inst_hub_1_reg15_21));
  or or_4 (rgb_video_1_p1, Button_4_out, s_r_ff_1_q);
  Button Button_4 (.out(Button_4_out));
  S_R_Flip_Flop s_r_ff_1 (
    .clk(rgb_video_1_p3[1]), .Q(s_r_ff_1_q), .reset(clock_3_out), .preset(rgb_video_1_p3[1]));  // open: S, R, Qn
  or or_5 (or_5_out, activ, inst_hub_1_reg7_14);
  Bit_Extender #(.out_width(5)) bit_extender_4 (.in(counter_3_q), .out(rgb_video_1_p4));
  Bit_Extender #(.out_width(5)) bit_extender_5 (.in(counter_4_q), .out(rgb_video_1_p5));
  DipSwitch DipSwitch_2 (
    .sw1(DipSwitch_1_sw24[31]), .sw2(DipSwitch_1_sw24[30]), .sw3(DipSwitch_1_sw24[29]),
    .sw4(DipSwitch_1_sw24[28]), .sw5(DipSwitch_1_sw24[27]), .sw6(DipSwitch_1_sw24[26]),
    .sw7(DipSwitch_1_sw24[25]), .sw8(DipSwitch_1_sw24[24]));
  // Probe on DipSwitch_1_sw24
  Button Button_3 ();  // open: out
  regnew regnew_1 (
    .regwritesel(multiplexer_7_out), .fggg(crg), .regasel(multiplexer_5_out), .Input_1(clk),
    .data(multiplexer_8_out), .regbsel(multiplexer_6_out), .aout(regnew_1_aout), .bout(regnew_1_bout));
  Multiplexer #(.select(2), .width(16)) multiplexer_8 (
    .in0(summ_1_resultout), .in1(bits16_31), .in2(RAM_1_dout), .in3(I_port), .out(multiplexer_8_out),
    .sel(inst_hub_1_reg_data_cntrl));
  inst_hub inst_hub_1 (
    .instr_inp(bits48_51), .reg0_6(inst_hub_1_reg0_6), .reg7_14(inst_hub_1_reg7_14),
    .reg15_21(inst_hub_1_reg15_21), .b_alu(b_alu), .progcount_jmp(pc_jmp), .brnh_on(brnh_on),
    .ram_addr(ram_addr), .ram_write(ram_write), .io_reg(IO_reg), .io_port(inst_hub_1_io_port),
    .I_port_on(I_port_on), .hlt(hlt), .crg(crg), .reg_data_cntrl(inst_hub_1_reg_data_cntrl),
    .datamode_cntrl(datamode_bus));
  DipSwitch #(.number(24)) DipSwitch_1 (
    .sw1(DipSwitch_1_sw24[23]), .sw2(DipSwitch_1_sw24[22]), .sw3(DipSwitch_1_sw24[21]),
    .sw4(DipSwitch_1_sw24[20]), .sw5(DipSwitch_1_sw24[19]), .sw6(DipSwitch_1_sw24[18]),
    .sw7(DipSwitch_1_sw24[17]), .sw8(DipSwitch_1_sw24[16]), .sw9(DipSwitch_1_sw24[15]),
    .sw10(DipSwitch_1_sw24[14]), .sw11(DipSwitch_1_sw24[13]), .sw12(DipSwitch_1_sw24[12]),
    .sw13(DipSwitch_1_sw24[11]), .sw14(DipSwitch_1_sw24[10]), .sw15(DipSwitch_1_sw24[9]),
    .sw16(DipSwitch_1_sw24[8]), .sw17(DipSwitch_1_sw24[7]), .sw18(DipSwitch_1_sw24[6]),
    .sw19(DipSwitch_1_sw24[5]), .sw20(DipSwitch_1_sw24[4]), .sw21(DipSwitch_1_sw24[3]),
    .sw22(DipSwitch_1_sw24[2]), .sw23(DipSwitch_1_sw24[1]), .sw24(DipSwitch_1_sw24[0]));
  assign bit_extender_6_out = {{4{bits60_63[3]}}, bits60_63};  // Bit_Extender bit_extender_6
  Counter counter_3 (
    .load(multiplexer_9_out), .D(demultiplexer_1_out1), .Q(counter_3_q), .up(1'b1), .clk(multiplexer_9_out));  // open: count, carry, clr
  Multiplexer multiplexer_9 (.in0(1'b0), .in1(clk), .out(multiplexer_9_out), .sel(or_6_out));
  or or_6 (or_6_out, demultiplexer_1_out1[0], demultiplexer_1_out1[1], demultiplexer_1_out1[2], demultiplexer_1_out1[3], demultiplexer_1_out1[4], demultiplexer_1_out1[5], demultiplexer_1_out1[6], demultiplexer_1_out1[7]);
  DipSwitch DipSwitch_3 (
    .sw1(DipSwitch_3_sw8[7]), .sw2(DipSwitch_3_sw8[6]), .sw3(DipSwitch_3_sw8[5]), .sw4(DipSwitch_3_sw8[4]),
    .sw5(DipSwitch_3_sw8[3]), .sw6(DipSwitch_3_sw8[2]), .sw7(DipSwitch_3_sw8[1]), .sw8(DipSwitch_3_sw8[0]));
  or or_7 (or_7_out, comparator_4_eq, comparator_2_eq);
  Multiplexer #(.width(16)) multiplexer_10 (
    .in0(regnew_1_bout), .in1(bits16_31), .out(multiplexer_10_out), .sel(or_8_out));
  or or_8 (or_8_out, or_7_out, b_alu);
  Multiplexer multiplexer_11 (.in0(1'b0), .in1(clk), .out(clk));  // open: sel
  Counter counter_4 (
    .load(multiplexer_12_out), .D(demultiplexer_1_out2), .Q(counter_4_q), .up(1'b1), .clk(multiplexer_12_out));  // open: count, carry, clr
  Multiplexer multiplexer_12 (.in0(1'b0), .in1(clk), .out(multiplexer_12_out), .sel(or_9_out));
  or or_9 (or_9_out, demultiplexer_1_out2[0], demultiplexer_1_out2[1], demultiplexer_1_out2[2], demultiplexer_1_out2[3], demultiplexer_1_out2[4], demultiplexer_1_out2[5], demultiplexer_1_out2[6], demultiplexer_1_out2[7]);
  // Probe on DipSwitch_3_sw8
  Comparator comparator_1 (.a(bit_extender_6_out), .b(8'h6), .eq(comparator_1_eq));  // open: gt, lt
  Comparator comparator_2 (.a(bit_extender_6_out), .b(8'h1), .eq(comparator_2_eq));  // open: gt, lt
  Comparator comparator_3 (.a(bit_extender_6_out), .b(8'h5), .eq(activ));  // open: gt, lt
  Comparator comparator_4 (.a(bit_extender_6_out), .b(8'h4), .eq(comparator_4_eq));  // open: gt, lt
  // Probe on multiplexer_10_out
  Multiplexer #(.width(16)) multiplexer_13 (
    .in0({16{1'b0}}), .in1(bits0_15), .out(multiplexer_13_out), .sel(inst_hub_1_io_port));
  // Probe on demultiplexer_1_out1
  // Probe on demultiplexer_1_out2
  // Probe on rgb_video_1_p3
  // Probe on regnew_1_aout
  summ summ_1 (
    .datain1(regnew_1_aout), .datain2(multiplexer_10_out), .datamode(datamode_bus), .plus(summ_1_plus),
    .minus(summ_1_minus), .zero(summ_1_zero), .regaout(summ_1_regaout), .regbout(summ_1_regbout),
    .resultout(summ_1_resultout));  // open: carry
  Multiplexer #(.select(2)) multiplexer_14 (
    .in0(summ_1_zero), .in1(summ_1_zero), .in2(summ_1_plus), .in3(summ_1_minus), .out(zero_flag),
    .sel(bits60_63[1:0]));
  Multiplexer #(.width(16)) multiplexer_15 (
    .in0(summ_1_regaout), .in1(summ_1_regbout), .out(multiplexer_15_out), .sel(comparator_4_eq));
  Multiplexer #(.width(16)) multiplexer_16 (
    .in0(RAM_1_dout), .in1(summ_1_regbout), .out(multiplexer_16_out), .sel(IO_reg));
  Bit_Extender #(.in_width(16), .out_width(8), .\type ("zero")) bit_extender_7 (
    .in(multiplexer_16_out), .out(bit_extender_7_out));
  Demultiplexer #(.select(4), .width(8)) demultiplexer_1 (
    .out1(demultiplexer_1_out1), .out2(demultiplexer_1_out2), .out3(rgb_video_1_p3), .out4(terminal_clear),
    .out5(terminal_acii), .in(bit_extender_7_out), .sel(multiplexer_13_out[3:0]));  // open: out0, out6, out7, out8, out9, out10, out11, out12, out13, out14, out15
  Multiplexer #(.width(16)) multiplexer_17 (
    .in0(bits16_31), .in1(summ_1_regbout), .out(multiplexer_17_out), .sel(activ));
  or or_10 (or_10_out, ram_write, ram_addr);
  Multiplexer #(.width(16)) multiplexer_18 (
    .in0({16{1'b0}}), .in1(multiplexer_17_out), .out(multiplexer_18_out), .sel(or_10_out));
  Multiplexer #(.width(16)) multiplexer_19 (
    .in0({16{1'b0}}), .in1(bits0_15), .out(multiplexer_19_out), .sel(I_port_on));
  // Probe on joystick_1_x
  Joystick #(.bits(5)) joystick_1 (.x(joystick_1_x), .y(joystick_1_y));
  // Probe on joystick_1_y
  Multiplexer multiplexer_20 (.in0(1'b0), .in1(clk), .out(multiplexer_20_out), .sel(ram_write));
  Bit_Extender #(.in_width(16), .out_width(4), .\type ("zero")) bit_extender_8 (
    .in(multiplexer_19_out), .out(bit_extender_8_out));
  assign bit_extender_9_out = {{11{1'b0}}, joystick_1_x};  // Bit_Extender bit_extender_9
  assign bit_extender_10_out = {{11{1'b0}}, joystick_1_y};  // Bit_Extender bit_extender_10
  RAM #(.addrWidth(16), .dataWidth(16), .trigger("high")) RAM_1 (
    .addr(multiplexer_18_out), .we(multiplexer_20_out), .oe(1'b1), .din(multiplexer_21_out), .dout(RAM_1_dout));
  Multiplexer #(.width(16)) multiplexer_21 (
    .in0(multiplexer_15_out), .in1(bits0_15), .out(multiplexer_21_out), .sel(comparator_1_eq));
  Multiplexer #(.select(4), .width(16)) multiplexer_22 (
    .in0({16{1'b0}}), .in1(bit_extender_9_out), .in2(bit_extender_10_out), .in3(undriven_3),
    .in4(keyboard_acii_inp), .out(I_port), .sel(bit_extender_8_out));  // open: in5, in6, in7, in8, in9, in10, in11, in12, in13, in14, in15
  // also tied to GND on the sheet: multiplexer_4_out

  // Notes on the sheet:
  //   contents of ROM_1 (hex, n*v repeats v):
  //   0 e000000000001 b000000020003 1003000500060005 1003000600040006 1003000300000000 1003000400000000
  //   2006000a00050003 2000900030005 5000b00000000 2000900050003 2006000e00060004 2000a00040006
  //   5000f00000000 2000a00060004 3006001200050003 40007ffff0007 5001300000000 4000700010007
  //   3006001600060004 40008ffff0008 5001700000000 4000800010008 2000b000a0009 0 9000000030001
  //   9000000040002 b000000010003 6001e00050003 5001f00000000 6002b00060004 1000c000b000b 20001000a0000
  //   200600280001000c 5002600000000 1000b0009000b 1000400080004 5001800000000 300600230009000c
  //   5001800000000 2000b000a000b 1000300070003 5002600000000 5000000000000 d000000000001 d000000000001
endmodule

module trigger (
  input  [23:0] inp1,
  input  write2,
  input  reset2,
  input  [23:0] input1,
  input  write1,
  input  dreset,
  output [23:0] Output_bus_1,
  output [23:0] Output_bus_2
);

  Register #(.width(24)) register_1 (.D(inp1), .en(write2), .clk(write2), .Q(Output_bus_1), .clr(reset2));
  Register #(.width(24)) register_2 (.D(input1), .en(write1), .clk(write1), .Q(Output_bus_2), .clr(dreset));
endmodule

module summ (
  input  [15:0] datain1,
  input  [15:0] datain2,
  input  [2:0] datamode,
  output plus,
  output minus,
  output zero,
  output carry,
  output [15:0] regaout,
  output [15:0] regbout,
  output [15:0] resultout
);

  wire [15:0] adder_1_out, subtractor_1_out;

  Comparator #(.width(16)) comparator_1 (.a(datain1), .b(datain2), .eq(zero));  // open: gt, lt
  Comparator #(.width(16)) comparator_2 (.a(datain2), .b(datain1), .gt(minus), .lt(plus));  // open: eq
  Adder #(.width(16)) adder_1 (.a(datain1), .b(datain2), .out(adder_1_out));  // open: cin, cout
  Subtractor #(.width(16)) subtractor_1 (.a(datain1), .b(datain2), .out(subtractor_1_out), .bout(carry));  // open: bin
  Multiplexer #(.select(3), .width(16)) multiplexer_1 (
    .in0({16{1'b0}}), .in1(adder_1_out), .in2(subtractor_1_out), .out(resultout), .sel(datamode));  // open: in3, in4, in5, in6, in7

  assign regaout = datain1;
  assign regbout = datain2;
endmodule

module reg1 (
  input  [4:0] inp,
  input  rg,
  input  cr,
  output [4:0] out_4
);

  Register #(.width(5)) register_1 (.D(inp), .en(rg), .clk(rg), .Q(out_4), .clr(cr));
endmodule

module compiller (
  input  [7:0] in_1,
  input  [7:0] in_2,
  input  in_3,
  input  in_4,
  input  in_5,
  input  in_6,
  input  in_7,
  input  in_8,
  input  in_9,
  input  in_10,
  input  in_11,
  input  in_12,
  input  in_13,
  input  in_14,
  input  in_15,
  input  in_16,
  input  in_17,
  input  in_18,
  input  in_19,
  input  in_20,
  input  in_21,
  input  in_22,
  input  in_23,
  input  in_24,
  input  in_25,
  input  in_26,
  input  in_27,
  input  in_28,
  input  in_29,
  input  in_30,
  input  in_31,
  input  in_32,
  input  in_33,
  input  in_34,
  input  in_35,
  input  in_36,
  input  in_37,
  input  in_38,
  input  in_39,
  input  in_40,
  input  in_41,
  input  in_42,
  input  in_43,
  input  in_44,
  input  in_45,
  input  in_46,
  input  in_47,
  input  in_48,
  input  in_49,
  input  in_50,
  input  in_51,
  input  in_52,
  input  in_53,
  input  in_54,
  input  in_55,
  input  in_56,
  input  in_57,
  input  in_58,
  input  in_59,
  input  in_60,
  input  in_61,
  input  in_62,
  input  in_63,
  input  in_64
);

  wire [4:0] bit_extender_1_out, bit_extender_2_out;

  Bit_Extender #(.out_width(5)) bit_extender_1 (.in(in_1), .out(bit_extender_1_out));
  Decoder #(.enable("false"), .select(5)) decoder_1 (
    .out1(in_3), .out2(in_4), .out3(in_5), .out4(in_6), .out5(in_7), .out6(in_8), .out7(in_9), .out8(in_10),
    .out9(in_11), .out10(in_12), .out11(in_13), .out12(in_14), .out13(in_15), .out14(in_16), .out15(in_17),
    .out16(in_18), .out17(in_19), .out18(in_20), .out19(in_21), .out20(in_22), .out21(in_23), .out22(in_24),
    .out23(in_25), .out24(in_26), .out25(in_27), .out26(in_28), .out27(in_29), .out28(in_30), .out29(in_31),
    .out30(in_32), .out31(in_33), .sel(bit_extender_1_out));  // open: out0
  Bit_Extender #(.out_width(5)) bit_extender_2 (.in(in_2), .out(bit_extender_2_out));
  Decoder #(.enable("false"), .select(5)) decoder_2 (
    .out1(in_34), .out2(in_35), .out3(in_36), .out4(in_37), .out5(in_38), .out6(in_39), .out7(in_40),
    .out8(in_41), .out9(in_42), .out10(in_43), .out11(in_44), .out12(in_45), .out13(in_46), .out14(in_47),
    .out15(in_48), .out16(in_49), .out17(in_50), .out18(in_51), .out19(in_52), .out20(in_53), .out21(in_54),
    .out22(in_55), .out23(in_56), .out24(in_57), .out25(in_58), .out26(in_59), .out27(in_60), .out28(in_61),
    .out29(in_62), .out30(in_63), .out31(in_64), .sel(bit_extender_2_out));  // open: out0
endmodule

module bitdetector8 (
  input  [7:0] in_1,
  output out_2
);

  or or_1 (out_2, in_1[0], in_1[1], in_1[2], in_1[3], in_1[5], in_1[6], in_1[7], in_1[4]);
endmodule

module hub (
  input  [7:0] otpo,
  output one,
  output Output_1,
  output Output_2,
  output Output_3,
  output Output_4,
  output Output_5,
  output Output_6,
  output Output_7,
  output Output_8,
  output Output_9,
  output Output_10,
  output Output_11,
  output Output_12,
  output Output_13,
  output Output_14,
  output Output_15,
  output Output_16,
  output Output_17,
  output Output_18,
  output Output_19,
  output Output_20,
  output Output_21,
  output Output_22,
  output Output_23,
  output Output_24,
  output Output_25,
  output Output_26,
  output Output_27,
  output Output_28,
  output Output_29,
  output Output_30
);

  wire [4:0] bit_extender_1_out;

  Bit_Extender #(.out_width(5)) bit_extender_1 (.in(otpo), .out(bit_extender_1_out));
  Decoder #(.enable("false"), .select(5)) decoder_1 (
    .out1(one), .out2(Output_1), .out3(Output_2), .out4(Output_3), .out5(Output_4), .out6(Output_5),
    .out7(Output_6), .out8(Output_7), .out9(Output_8), .out10(Output_9), .out11(Output_10),
    .out12(Output_11), .out13(Output_12), .out14(Output_13), .out15(Output_14), .out16(Output_15),
    .out17(Output_16), .out18(Output_17), .out19(Output_18), .out20(Output_19), .out21(Output_20),
    .out22(Output_21), .out23(Output_22), .out24(Output_23), .out25(Output_24), .out26(Output_25),
    .out27(Output_26), .out28(Output_27), .out29(Output_28), .out30(Output_29), .out31(Output_30),
    .sel(bit_extender_1_out));  // open: out0
endmodule

module bitdetector6 (
  input  [5:0] in_1,
  output out_2
);

  or or_1 (out_2, in_1[0], in_1[1], in_1[2], in_1[3], in_1[4], in_1[5]);
endmodule

module bitdetector2 (
  input  [1:0] in_1,
  output out_2
);

  or or_1 (out_2, in_1[0], in_1[1]);
endmodule

module bitdetectornob08 (
  input  [7:0] data,
  input  [7:0] dataforignore,
  input  enableinput,
  output outpt
);

  wire comparator_1_gt, comparator_1_lt, or_1_out;

  and and_1 (outpt, or_1_out, enableinput);
  Comparator comparator_1 (.a(dataforignore), .b(data), .gt(comparator_1_gt), .lt(comparator_1_lt));  // open: eq
  or or_1 (or_1_out, comparator_1_gt, comparator_1_lt);
endmodule

module bitdetectornb6 (
  input  [5:0] in_1,
  output out_2
);

  wire comparator_1_eq, or_1_out;

  Comparator #(.width(6)) comparator_1 (.a({6{1'b1}}), .b(in_1), .eq(comparator_1_eq));  // open: gt, lt
  or or_1 (or_1_out, in_1[0], in_1[1], in_1[2], in_1[4], in_1[5], in_1[3]);
  Multiplexer multiplexer_1 (.in0(or_1_out), .in1(1'b0), .out(out_2), .sel(comparator_1_eq));
endmodule

module offset (
  input  a,
  output otu
);

  wire not_1_out;

  and and_1 (otu, a, not_1_out);
  not not_1 (not_1_out, a);
endmodule

module bitdetectorno3 (
  input  [7:0] in_1,
  output out_2
);

  wire comparator_1_eq, or_1_out;
  wire [2:0] bit_extender_1_out;

  Bit_Extender #(.out_width(3)) bit_extender_1 (.in(in_1), .out(bit_extender_1_out));
  Comparator comparator_1 (.a({8{1'b1}}), .b(in_1), .eq(comparator_1_eq));  // open: gt, lt
  or or_1 (or_1_out, bit_extender_1_out[1], bit_extender_1_out[2], bit_extender_1_out[0]);
  Multiplexer multiplexer_1 (.in0(or_1_out), .in1(1'b0), .out(out_2), .sel(comparator_1_eq));
endmodule

module buttoncontrol (
  input  sinin,
  input  [7:0] firstinp,
  input  [7:0] in_3,
  input  [7:0] in_4,
  input  [7:0] in_5,
  input  [7:0] in_6,
  input  [7:0] in_7,
  input  [7:0] in_8,
  input  [7:0] in_9,
  input  [7:0] in_10,
  input  [7:0] in_11,
  input  [7:0] in_12,
  input  [7:0] in_13,
  output [7:0] outsim
);

  wire [3:0] counter_1_q;

  Counter #(.max('hb), .width(4)) counter_1 (
    .count(sinin), .Q(counter_1_q), .clk(sinin));  // open: load, D, carry, up, clr
  Multiplexer #(.select(4), .width(8)) multiplexer_1 (
    .in0(firstinp), .in1(in_3), .in2(in_4), .in3(in_5), .in4(in_6), .in5(in_7), .in6(in_8), .in7(in_9),
    .in8(in_10), .in9(in_11), .in10(in_12), .in11(in_13), .out(outsim), .sel(counter_1_q));  // open: in12, in13, in14, in15
endmodule

module buttonouter (
  input  inp1,
  input  in_2,
  input  in_3,
  input  in_4,
  input  in_5,
  input  in_6,
  input  in_7,
  input  in_8,
  input  in_9,
  input  in_10,
  input  in_11,
  input  in_12,
  input  in_13,
  input  in_14,
  input  in_15,
  input  in_16,
  input  [7:0] in12,
  input  [7:0] in_18,
  input  [7:0] in_19,
  input  [7:0] in_20,
  input  [7:0] in_21,
  input  [7:0] in_22,
  input  [7:0] in_23,
  input  [7:0] in_24,
  input  [7:0] in_25,
  input  [7:0] in_26,
  input  [7:0] in_27,
  input  [7:0] in_28,
  input  [7:0] in_29,
  input  [7:0] in_30,
  input  [7:0] in_31,
  input  [7:0] in_32,
  output [7:0] out1,
  output [7:0] out_34,
  output [7:0] out_35,
  output [7:0] out_36,
  output [7:0] out_37,
  output [7:0] out_38,
  output [7:0] out_39,
  output [7:0] out_40,
  output [7:0] out_41,
  output [7:0] out_42,
  output [7:0] out_43,
  output [7:0] out_44,
  output [7:0] out_45,
  output [7:0] out_46,
  output [7:0] out_47,
  output [7:0] out_48
);

  Multiplexer #(.width(8)) multiplexer_1 (.in0({8{1'b0}}), .in1(in12), .out(out1), .sel(inp1));
  Multiplexer #(.width(8)) multiplexer_2 (.in0({8{1'b0}}), .in1(in_18), .out(out_34), .sel(in_2));
  Multiplexer #(.width(8)) multiplexer_3 (.in0({8{1'b0}}), .in1(in_19), .out(out_35), .sel(in_3));
  Multiplexer #(.width(8)) multiplexer_4 (.in0({8{1'b0}}), .in1(in_20), .out(out_36), .sel(in_4));
  Multiplexer #(.width(8)) multiplexer_5 (.in0({8{1'b0}}), .in1(in_21), .out(out_37), .sel(in_5));
  Multiplexer #(.width(8)) multiplexer_6 (.in0({8{1'b0}}), .in1(in_22), .out(out_38), .sel(in_6));
  Multiplexer #(.width(8)) multiplexer_7 (.in0({8{1'b0}}), .in1(in_23), .out(out_39), .sel(in_7));
  Multiplexer #(.width(8)) multiplexer_8 (.in0({8{1'b0}}), .in1(in_24), .out(out_40), .sel(in_8));
  Multiplexer #(.width(8)) multiplexer_9 (.in0({8{1'b0}}), .in1(in_25), .out(out_41), .sel(in_9));
  Multiplexer #(.width(8)) multiplexer_10 (.in0({8{1'b0}}), .in1(in_26), .out(out_42), .sel(in_10));
  Multiplexer #(.width(8)) multiplexer_11 (.in0({8{1'b0}}), .in1(in_27), .out(out_43), .sel(in_11));
  Multiplexer #(.width(8)) multiplexer_12 (.in0({8{1'b0}}), .in1(in_28), .out(out_44), .sel(in_12));
  Multiplexer #(.width(8)) multiplexer_13 (.in0({8{1'b0}}), .in1(in_29), .out(out_45), .sel(in_13));
  Multiplexer #(.width(8)) multiplexer_14 (.in0({8{1'b0}}), .in1(in_30), .out(out_46), .sel(in_14));
  Multiplexer #(.width(8)) multiplexer_15 (.in0({8{1'b0}}), .in1(in_32), .out(out_48), .sel(in_16));
  Multiplexer #(.width(8)) multiplexer_16 (.in0({8{1'b0}}), .in1(in_31), .out(out_47), .sel(in_15));
endmodule

module trigger24bit (
  input  [23:0] inp1,
  input  [23:0] input1,
  output [23:0] out_3,
  output [23:0] out_4
);

  wire bitdetector8_1_out_2, bitdetector8_2_out_2, bitdetectornob08_1_outpt, bitdetectornob08_2_outpt;
  wire [7:0] bit_extender_1_out, bit_extender_2_out;

  Bit_Extender #(.in_width(24), .out_width(8)) bit_extender_1 (.in(inp1), .out(bit_extender_1_out));
  Bit_Extender #(.in_width(24), .out_width(8), .\type ("zero")) bit_extender_2 (.in(input1), .out(bit_extender_2_out));
  bitdetector8 bitdetector8_1 (.in_1(bit_extender_1_out), .out_2(bitdetector8_1_out_2));
  bitdetectornob08 bitdetectornob08_1 (
    .enableinput(bitdetector8_1_out_2), .data(bit_extender_1_out), .dataforignore({8{1'b1}}),
    .outpt(bitdetectornob08_1_outpt));
  bitdetector8 bitdetector8_2 (.in_1(bit_extender_2_out), .out_2(bitdetector8_2_out_2));
  bitdetectornob08 bitdetectornob08_2 (
    .enableinput(bitdetector8_2_out_2), .data(bit_extender_2_out), .dataforignore({8{1'b1}}),
    .outpt(bitdetectornob08_2_outpt));
  Register #(.width(24)) register_1 (
    .D(inp1), .en(bitdetectornob08_1_outpt), .clk(bitdetectornob08_1_outpt), .Q(out_3));  // open: clr
  Register #(.width(24)) register_2 (
    .D(input1), .en(bitdetectornob08_2_outpt), .clk(bitdetectornob08_2_outpt), .Q(out_4));  // open: clr
endmodule

module bit48to_2_24 (
  input  [51:0] inp,
  output [23:0] out1_data_24,
  output [23:0] out2_data_24,
  output [3:0] opcode_4
);


  assign opcode_4 = inp[51:48];
  assign out1_data_24 = inp[23:0];
  assign out2_data_24 = inp[47:24];
endmodule

module t24_to_2_8_1_op_8 (
  input  [23:0] inp_24,
  output [7:0] out1_8,
  output [7:0] out2_8,
  output [7:0] out3_8
);


  assign out1_8 = inp_24[7:0];
  assign out2_8 = inp_24[15:8];
  assign out3_8 = inp_24[23:16];
endmodule

module instr_rom (
  input  [3:0] inp4,
  output [2:0] out3,
  output outinstr3,
  output instr_out_5,
  output instr_out_7,
  output instr_out_6,
  output instr_out_10,
  output instr_out_9,
  output instr_out_11
);

  wire demultiplexer_1_out1, demultiplexer_1_out2, demultiplexer_1_out4, demultiplexer_1_out8, or_1_out;
  wire [2:0] multiplexer_1_out, multiplexer_2_out, multiplexer_3_out, multiplexer_4_out;

  or or_1 (or_1_out, instr_out_10, demultiplexer_1_out1, instr_out_5, instr_out_9);
  Demultiplexer #(.select(4)) demultiplexer_1 (
    .out1(demultiplexer_1_out1), .out2(demultiplexer_1_out2), .out3(outinstr3), .out4(demultiplexer_1_out4),
    .out5(instr_out_5), .out6(instr_out_6), .out7(instr_out_7), .out8(demultiplexer_1_out8),
    .out9(instr_out_9), .out10(instr_out_10), .out11(instr_out_11), .in(1'b1), .sel(inp4));  // open: out0, out12, out13, out14, out15
  Multiplexer #(.width(3)) multiplexer_1 (.in0(3'b000), .in1(3'b001), .out(multiplexer_1_out), .sel(or_1_out));
  Multiplexer #(.width(3)) multiplexer_2 (
    .in0(3'b000), .in1(3'b010), .out(multiplexer_2_out), .sel(demultiplexer_1_out2));
  Multiplexer #(.width(3)) multiplexer_3 (
    .in0(3'b000), .in1(3'b011), .out(multiplexer_3_out), .sel(demultiplexer_1_out4));
  Multiplexer #(.width(3)) multiplexer_4 (
    .in0(3'b000), .in1(3'b100), .out(multiplexer_4_out), .sel(demultiplexer_1_out8));
  assign out3 = multiplexer_1_out | multiplexer_2_out | multiplexer_3_out | multiplexer_4_out;  // OR_Gate or_2, 3 bits wide
endmodule

module regnew (
  input  fggg,
  input  Input_1,
  input  [15:0] data,
  input  [15:0] regbsel,
  input  [15:0] regasel,
  input  [15:0] regwritesel,
  output [15:0] aout,
  output [15:0] bout
);

  wire demultiplexer_1_out1, demultiplexer_1_out2, demultiplexer_1_out3, demultiplexer_1_out4,
       demultiplexer_1_out5, demultiplexer_1_out6, demultiplexer_1_out7, demultiplexer_1_out8,
       demultiplexer_1_out9, demultiplexer_1_out10, demultiplexer_1_out11, demultiplexer_1_out12,
       demultiplexer_1_out13, demultiplexer_1_out14, demultiplexer_1_out15;
  wire [3:0] bit_extender_1_out, bit_extender_2_out, bit_extender_3_out;
  wire [15:0] counter_1_q, counter_2_q, counter_3_q, counter_4_q, counter_5_q, counter_6_q, counter_7_q,
       counter_8_q, counter_9_q, counter_10_q, counter_11_q, counter_12_q, counter_13_q, counter_14_q,
       counter_15_q, demultiplexer_2_out1, demultiplexer_2_out2, demultiplexer_2_out3, demultiplexer_2_out4,
       demultiplexer_2_out5, demultiplexer_2_out6, demultiplexer_2_out7, demultiplexer_2_out8,
       demultiplexer_2_out9, demultiplexer_2_out10, demultiplexer_2_out11, demultiplexer_2_out12,
       demultiplexer_2_out13, demultiplexer_2_out14, demultiplexer_2_out15;

  Bit_Extender #(.in_width(16), .out_width(4), .\type ("zero")) bit_extender_1 (
    .in(regwritesel), .out(bit_extender_1_out));
  Demultiplexer #(.select(4)) demultiplexer_1 (
    .out1(demultiplexer_1_out1), .out2(demultiplexer_1_out2), .out3(demultiplexer_1_out3),
    .out4(demultiplexer_1_out4), .out5(demultiplexer_1_out5), .out6(demultiplexer_1_out6),
    .out7(demultiplexer_1_out7), .out8(demultiplexer_1_out8), .out9(demultiplexer_1_out9),
    .out10(demultiplexer_1_out10), .out11(demultiplexer_1_out11), .out12(demultiplexer_1_out12),
    .out13(demultiplexer_1_out13), .out14(demultiplexer_1_out14), .out15(demultiplexer_1_out15),
    .in(Input_1), .sel(bit_extender_1_out));  // open: out0
  Demultiplexer #(.select(4), .width(16)) demultiplexer_2 (
    .out1(demultiplexer_2_out1), .out2(demultiplexer_2_out2), .out3(demultiplexer_2_out3),
    .out4(demultiplexer_2_out4), .out5(demultiplexer_2_out5), .out6(demultiplexer_2_out6),
    .out7(demultiplexer_2_out7), .out8(demultiplexer_2_out8), .out9(demultiplexer_2_out9),
    .out10(demultiplexer_2_out10), .out11(demultiplexer_2_out11), .out12(demultiplexer_2_out12),
    .out13(demultiplexer_2_out13), .out14(demultiplexer_2_out14), .out15(demultiplexer_2_out15), .in(data),
    .sel(bit_extender_1_out));  // open: out0
  Counter #(.max('hffff), .width(16)) counter_1 (
    .load(demultiplexer_1_out1), .D(demultiplexer_2_out1), .Q(counter_1_q), .clk(demultiplexer_1_out1),
    .clr(fggg));  // open: count, carry, up
  Counter #(.max('hffff), .width(16)) counter_2 (
    .load(demultiplexer_1_out2), .D(demultiplexer_2_out2), .Q(counter_2_q), .clk(demultiplexer_1_out2),
    .clr(fggg));  // open: count, carry, up
  Counter #(.max('hffff), .width(16)) counter_3 (
    .load(demultiplexer_1_out3), .D(demultiplexer_2_out3), .Q(counter_3_q), .clk(demultiplexer_1_out3),
    .clr(fggg));  // open: count, carry, up
  Counter #(.max('hffff), .width(16)) counter_4 (
    .load(demultiplexer_1_out4), .D(demultiplexer_2_out4), .Q(counter_4_q), .clk(demultiplexer_1_out4),
    .clr(fggg));  // open: count, carry, up
  Counter #(.max('hffff), .width(16)) counter_5 (
    .load(demultiplexer_1_out5), .D(demultiplexer_2_out5), .Q(counter_5_q), .clk(demultiplexer_1_out5),
    .clr(fggg));  // open: count, carry, up
  Counter #(.max('hffff), .width(16)) counter_6 (
    .load(demultiplexer_1_out6), .D(demultiplexer_2_out6), .Q(counter_6_q), .clk(demultiplexer_1_out6),
    .clr(fggg));  // open: count, carry, up
  Counter #(.max('hffff), .width(16)) counter_7 (
    .load(demultiplexer_1_out7), .D(demultiplexer_2_out7), .Q(counter_7_q), .clk(demultiplexer_1_out7),
    .clr(fggg));  // open: count, carry, up
  Counter #(.max('hffff), .width(16)) counter_8 (
    .load(demultiplexer_1_out8), .D(demultiplexer_2_out8), .Q(counter_8_q), .clk(demultiplexer_1_out8),
    .clr(fggg));  // open: count, carry, up
  Counter #(.max('hffff), .width(16)) counter_9 (
    .load(demultiplexer_1_out9), .D(demultiplexer_2_out9), .Q(counter_9_q), .clk(demultiplexer_1_out9),
    .clr(fggg));  // open: count, carry, up
  Counter #(.max('hffff), .width(16)) counter_10 (
    .load(demultiplexer_1_out10), .D(demultiplexer_2_out10), .Q(counter_10_q), .clk(demultiplexer_1_out10),
    .clr(fggg));  // open: count, carry, up
  Counter #(.max('hffff), .width(16)) counter_11 (
    .load(demultiplexer_1_out11), .D(demultiplexer_2_out11), .Q(counter_11_q), .clk(demultiplexer_1_out11),
    .clr(fggg));  // open: count, carry, up
  Counter #(.max('hffff), .width(16)) counter_12 (
    .load(demultiplexer_1_out12), .D(demultiplexer_2_out12), .Q(counter_12_q), .clk(demultiplexer_1_out12),
    .clr(fggg));  // open: count, carry, up
  Counter #(.max('hffff), .width(16)) counter_13 (
    .load(demultiplexer_1_out13), .D(demultiplexer_2_out13), .Q(counter_13_q), .clk(demultiplexer_1_out13),
    .clr(fggg));  // open: count, carry, up
  Counter #(.max('hffff), .width(16)) counter_14 (
    .load(demultiplexer_1_out14), .D(demultiplexer_2_out14), .Q(counter_14_q), .clk(demultiplexer_1_out14),
    .clr(fggg));  // open: count, carry, up
  Counter #(.max('hffff), .width(16)) counter_15 (
    .load(demultiplexer_1_out15), .D(demultiplexer_2_out15), .Q(counter_15_q), .clk(demultiplexer_1_out15),
    .clr(fggg));  // open: count, carry, up
  Multiplexer #(.select(4), .width(16)) multiplexer_1 (
    .in0({16{1'b0}}), .in1(counter_1_q), .in2(counter_2_q), .in3(counter_3_q), .in4(counter_4_q),
    .in5(counter_5_q), .in6(counter_6_q), .in7(counter_7_q), .in8(counter_8_q), .in9(counter_9_q),
    .in10(counter_10_q), .in11(counter_11_q), .in12(counter_12_q), .in13(counter_13_q), .in14(counter_14_q),
    .in15(counter_15_q), .out(aout), .sel(bit_extender_2_out));
  Multiplexer #(.select(4), .width(16)) multiplexer_2 (
    .in0({16{1'b0}}), .in1(counter_1_q), .in2(counter_2_q), .in3(counter_3_q), .in4(counter_4_q),
    .in5(counter_5_q), .in6(counter_6_q), .in7(counter_7_q), .in8(counter_8_q), .in9(counter_9_q),
    .in10(counter_10_q), .in11(counter_11_q), .in12(counter_12_q), .in13(counter_13_q), .in14(counter_14_q),
    .in15(counter_15_q), .out(bout), .sel(bit_extender_3_out));
  Bit_Extender #(.in_width(16), .out_width(4), .\type ("zero")) bit_extender_2 (.in(regasel), .out(bit_extender_2_out));
  Bit_Extender #(.in_width(16), .out_width(4), .\type ("zero")) bit_extender_3 (.in(regbsel), .out(bit_extender_3_out));
endmodule

module inst_hub (
  input  [3:0] instr_inp,
  output reg0_6,
  output reg7_14,
  output reg15_21,
  output b_alu,
  output progcount_jmp,
  output brnh_on,
  output ram_addr,
  output ram_write,
  output io_reg,
  output io_port,
  output I_port_on,
  output hlt,
  output crg,
  output [1:0] reg_data_cntrl,
  output [2:0] datamode_cntrl
);

  wire decoder_1_out1, decoder_1_out2, decoder_1_out3, decoder_1_out4, decoder_1_out5, decoder_1_out6,
       decoder_1_out7, decoder_1_out8, decoder_1_out9, decoder_1_out10, decoder_1_out11, decoder_1_out12,
       decoder_1_out13, decoder_1_out14;

  or or_1 (datamode_cntrl[1], decoder_1_out6, decoder_1_out2);
  or or_2 (datamode_cntrl[0], decoder_1_out4, decoder_1_out1);
  Decoder #(.select(4)) decoder_1 (
    .out1(decoder_1_out1), .out2(decoder_1_out2), .out3(decoder_1_out3), .out4(decoder_1_out4),
    .out5(decoder_1_out5), .out6(decoder_1_out6), .out7(decoder_1_out7), .out8(decoder_1_out8),
    .out9(decoder_1_out9), .out10(decoder_1_out10), .out11(decoder_1_out11), .out12(decoder_1_out12),
    .out13(decoder_1_out13), .out14(decoder_1_out14), .sel(instr_inp));  // open: out0, out15, en
  or or_3 (reg_data_cntrl[1], decoder_1_out7, decoder_1_out12);
  or or_4 (reg_data_cntrl[0], decoder_1_out12, decoder_1_out3);
  or or_5 (reg0_6, decoder_1_out1, decoder_1_out2, decoder_1_out4, decoder_1_out6, decoder_1_out8);
  or or_6 (reg7_14, decoder_1_out1, decoder_1_out2, decoder_1_out6, decoder_1_out9, decoder_1_out11);
  or or_7 (reg15_21, decoder_1_out1, decoder_1_out2, decoder_1_out3, decoder_1_out4, decoder_1_out7, decoder_1_out12);
  or or_8 (b_alu, decoder_1_out4, decoder_1_out11);
  buf or_9 (progcount_jmp, decoder_1_out5);  // OR_Gate
  buf or_10 (brnh_on, decoder_1_out6);  // OR_Gate
  or or_11 (ram_addr, decoder_1_out7, decoder_1_out10);
  buf or_12 (ram_write, decoder_1_out8);  // OR_Gate
  or or_13 (io_reg, decoder_1_out9, decoder_1_out11);
  or or_14 (io_port, decoder_1_out9, decoder_1_out10, decoder_1_out11);
  buf or_15 (I_port_on, decoder_1_out12);  // OR_Gate
  buf or_16 (hlt, decoder_1_out13);  // OR_Gate
  buf or_17 (crg, decoder_1_out14);  // OR_Gate

  assign datamode_cntrl[2] = 1'b0;
endmodule

module RRam (
  input  [15:0] ra,
  input  [15:0] rb,
  input  [15:0] in_3
);
endmodule
